# Fritzing sketch mpr121-inputs (saved by Fritzing 0.9.3b)

parts:
  Part1 = Adafruit MPR121
  Raspberry_Pi_1 = Raspberry Pi 3 [part_number=RPI-3-V1.2]

nets:
  GND: Part1.GND, Raspberry_Pi_1.GND
  VIN: Part1.VIN, Raspberry_Pi_1.3v3
  N1: Part1.SDA, Raspberry_Pi_1.GPIO2
  N2: Part1.SCL, Raspberry_Pi_1.GPIO3

custom parts:
  Adafruit MPR121: Add lots of touch sensors to your next microcontroller project with this easy-to-use 12-channel capacitive touch sensor breakout board, starring the MPR121. This chip can handle up to 12 individual touch pads. The MPR121 has support for only I2C, which can be implemented with nearly any microcontroller. You can select one of 4 addresses with the ADDR pin, for a total of 48 capacitive touch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
